// Digital circuit 16_bit_register.dig as structural Verilog
module _16_bit_register (
  input  INR,
  input  CLK,
  input  [15:0] Din,
  input  ld,
  input  clr,
  output [15:0] D
);

  CounterPreset #(.Bits(16)) counterpreset_1 (
    .en(INR), .C(CLK), .dir(1'b0), .in(Din), .ld(ld), .clr(clr), .out(D));  // open: ovf
endmodule
