// Digital circuit 8_bit_register.dig as structural Verilog
module _8_bit_register (
  input  INR,
  input  CLK,
  input  [7:0] Din,
  input  ld,
  input  clr,
  output [7:0] D
);

  CounterPreset #(.Bits(8)) counterpreset_1 (
    .en(INR), .C(CLK), .dir(1'b0), .in(Din), .ld(ld), .clr(clr), .out(D));  // open: ovf
endmodule
