// Digital circuit Memory_selection_logic.dig as structural Verilog
module Memory_selection_logic (
  output out_1
);

  wire and_1_out, and_2_out, and_3_out, and_4_out, and_5_out, and_6_out, D0, D1, D2, D6, D_7, I, R, T1, T3,
       T4;

  and and_1 (and_1_out, R, T1);
  and and_2 (and_2_out, D_7, I, T3);
  and and_3 (and_3_out, T4, D0);
  and and_4 (and_4_out, T4, D1);
  and and_5 (and_5_out, T4, D2);
  and and_6 (and_6_out, T4, D6);
  or or_1 (out_1, and_1_out, and_2_out, and_3_out, and_4_out, and_5_out, and_6_out);
endmodule
