// Digital circuit ac_control.dig as structural Verilog
module ac_control (
  output ld,
  output clr,
  output INR
);

  wire and_1_out, and_2_out, and_3_out, D0, D1, D2, D3, D4, or_1_out, or_2_out, P0, P1, P8, P9, P10, P12, q,
       r, T5;

  or or_1 (or_1_out, D0, D1, D2, D3, D4);
  or or_2 (or_2_out, P1, P12, P8, P9);
  and and_1 (and_1_out, or_1_out, T5);
  and and_2 (and_2_out, r, or_2_out);
  and and_3 (and_3_out, q, P0);
  and and_4 (INR, r, P10);
  and and_5 (clr, r, P0);
  or or_3 (ld, and_1_out, and_2_out, and_3_out);
endmodule
