// Digital circuit alu.dig as structural Verilog
module alu (
  input  [15:0] AC,
  input  [15:0] DR,
  input  [7:0] INPR,
  output Cout,
  output [15:0] ALUout
);

  wire alu_one_stage_1_c_i_plus_1, alu_one_stage_2_c_i_plus_1, alu_one_stage_3_c_i_plus_1,
       alu_one_stage_4_c_i_plus_1, alu_one_stage_5_c_i_plus_1, alu_one_stage_6_c_i_plus_1,
       alu_one_stage_7_c_i_plus_1, alu_one_stage_8_c_i_plus_1, alu_one_stage_8_ii,
       alu_one_stage_9_c_i_plus_1, alu_one_stage_10_c_i_plus_1, alu_one_stage_11_c_i_plus_1,
       alu_one_stage_12_c_i_plus_1, alu_one_stage_13_c_i_plus_1, alu_one_stage_14_c_i_plus_1,
       alu_one_stage_15_c_i_plus_1, and_1_out, and_2_out, E, P0, P12, q, r, undriven_2, undriven_3,
       undriven_4, undriven_5, undriven_7, undriven_8, undriven_9, undriven_10;
  wire [7:0] driver_1_out, driver_2_out, undriven_6;
  wire [15:0] sub_1_s;
  wire [15:3] undriven, undriven_11, undriven_12, undriven_13, undriven_14;

  and and_1 (and_1_out, q, P0);
  and and_2 (and_2_out, r, P12);
  assign driver_1_out = and_1_out ? INPR : 8'bz;  // Driver driver_1
  Sub #(.Bits(16)) sub_1 (
    .a({AC[15:12], AC[12], AC[10:4], AC[4], AC[2:0]}), .b(16'h1), .c_i(1'b0), .s(sub_1_s));  // open: c_o
  alu_one_stage alu_one_stage_1 (
    .Ii(undriven_6[6]), .C_i_plus_1(alu_one_stage_1_c_i_plus_1), .AC_i(AC[0]), .DR_i(DR[0]), .C_i(1'b0),
    .AC_i_plus_1(AC[1]), .AC_i_1(E));
  alu_one_stage alu_one_stage_2 (
    .Ii(undriven_6[5]), .C_i_plus_1(alu_one_stage_2_c_i_plus_1), .AC_i(AC[1]), .DR_i(DR[1]),
    .C_i(alu_one_stage_1_c_i_plus_1), .AC_i_plus_1(undriven_10), .AC_i_1(AC[0]));
  alu_one_stage alu_one_stage_3 (
    .Ii(undriven_6[4]), .C_i_plus_1(alu_one_stage_3_c_i_plus_1), .AC_i(AC[2]), .DR_i(DR[2]),
    .C_i(alu_one_stage_2_c_i_plus_1), .AC_i_plus_1(AC[4]), .AC_i_1(AC[1]));
  alu_one_stage alu_one_stage_4 (
    .Ii(undriven_6[3]), .C_i_plus_1(alu_one_stage_4_c_i_plus_1), .AC_i(AC[4]), .DR_i(DR[3]),
    .C_i(alu_one_stage_3_c_i_plus_1), .AC_i_plus_1(undriven_9), .AC_i_1(AC[2]));
  alu_one_stage alu_one_stage_5 (
    .Ii(undriven_6[2]), .C_i_plus_1(alu_one_stage_5_c_i_plus_1), .AC_i(AC[4]), .DR_i(DR[4]),
    .C_i(alu_one_stage_4_c_i_plus_1), .AC_i_plus_1(AC[5]), .AC_i_1(AC[4]));
  assign driver_2_out[0] = and_2_out ? sub_1_s[0] : 1'bz;  // Driver driver_2
  alu_one_stage alu_one_stage_6 (
    .Ii(undriven_6[1]), .C_i_plus_1(alu_one_stage_6_c_i_plus_1), .AC_i(AC[5]), .DR_i(DR[5]),
    .C_i(alu_one_stage_5_c_i_plus_1), .AC_i_plus_1(undriven_7), .AC_i_1(AC[4]));
  alu_one_stage alu_one_stage_7 (
    .Ii(undriven_6[0]), .C_i_plus_1(alu_one_stage_7_c_i_plus_1), .AC_i(AC[6]), .DR_i(DR[6]),
    .C_i(alu_one_stage_6_c_i_plus_1), .AC_i_plus_1(AC[7]), .AC_i_1(AC[5]));
  alu_one_stage alu_one_stage_8 (
    .Ii(alu_one_stage_8_ii), .C_i_plus_1(alu_one_stage_8_c_i_plus_1), .AC_i(AC[7]), .DR_i(DR[7]),
    .C_i(alu_one_stage_7_c_i_plus_1), .AC_i_plus_1(undriven_8), .AC_i_1(AC[6]));
  assign ALUout[7:0] = undriven_6 | driver_1_out | driver_2_out;  // Or or_1, 8 bits wide
  alu_one_stage alu_one_stage_9 (
    .Ii(ALUout[8]), .C_i_plus_1(alu_one_stage_9_c_i_plus_1), .AC_i(AC[8]), .DR_i(DR[8]),
    .C_i(alu_one_stage_8_c_i_plus_1), .AC_i_plus_1(undriven_4), .AC_i_1(AC[7]));
  alu_one_stage alu_one_stage_10 (
    .Ii(ALUout[9]), .C_i_plus_1(alu_one_stage_10_c_i_plus_1), .AC_i(AC[9]), .DR_i(DR[9]),
    .C_i(alu_one_stage_9_c_i_plus_1), .AC_i_plus_1(undriven_3), .AC_i_1(AC[8]));
  alu_one_stage alu_one_stage_11 (
    .Ii(ALUout[10]), .C_i_plus_1(alu_one_stage_11_c_i_plus_1), .AC_i(AC[10]), .DR_i(DR[10]),
    .C_i(alu_one_stage_10_c_i_plus_1), .AC_i_plus_1(AC[12]), .AC_i_1(AC[9]));
  alu_one_stage alu_one_stage_12 (
    .Ii(ALUout[11]), .C_i_plus_1(alu_one_stage_12_c_i_plus_1), .AC_i(AC[12]), .DR_i(DR[11]),
    .C_i(alu_one_stage_11_c_i_plus_1), .AC_i_plus_1(undriven_2), .AC_i_1(AC[10]));
  alu_one_stage alu_one_stage_13 (
    .Ii(ALUout[12]), .C_i_plus_1(alu_one_stage_13_c_i_plus_1), .AC_i(AC[12]), .DR_i(DR[12]),
    .C_i(alu_one_stage_12_c_i_plus_1), .AC_i_plus_1(AC[13]), .AC_i_1(AC[12]));
  alu_one_stage alu_one_stage_14 (
    .Ii(ALUout[13]), .C_i_plus_1(alu_one_stage_14_c_i_plus_1), .AC_i(AC[13]), .DR_i(DR[13]),
    .C_i(alu_one_stage_13_c_i_plus_1), .AC_i_plus_1(undriven_5), .AC_i_1(AC[12]));
  alu_one_stage alu_one_stage_15 (
    .Ii(ALUout[14]), .C_i_plus_1(alu_one_stage_15_c_i_plus_1), .AC_i(AC[14]), .DR_i(DR[14]),
    .C_i(alu_one_stage_14_c_i_plus_1), .AC_i_plus_1(AC[15]), .AC_i_1(AC[13]));
  alu_one_stage alu_one_stage_16 (
    .Ii(ALUout[15]), .C_i_plus_1(Cout), .AC_i(AC[15]), .DR_i(DR[15]), .C_i(alu_one_stage_15_c_i_plus_1),
    .AC_i_plus_1(E), .AC_i_1(AC[14]));
  // Pins of 2 and 3 bits meet at AC[2:0]
  // Pins of 2 and 3 bits meet at AC[9:7]
  // Pins of 3 and 16 bits meet at {undriven_14, AC[4], AC[2:1]}
  // Pins of 2 and 3 bits meet at {{2{AC[4]}}, AC[2]}
  // Pins of 3 and 16 bits meet at {undriven_12, AC[6:4]}
  // Pins of 2 and 3 bits meet at AC[6:4]
  // Pins of 3 and 16 bits meet at {undriven_11, AC[7:5]}
  // Pins of 2 and 3 bits meet at AC[8:6]
  // Pins of 3 and 16 bits meet at {undriven_13, AC[5:4], AC[4]}
  // Pins of 2 and 3 bits meet at AC[10:8]
  // Pins of 3 and 16 bits meet at {undriven, AC[12], AC[10:9]}
  // Pins of 2 and 3 bits meet at {{2{AC[12]}}, AC[10]}

  assign {AC[11], AC[3]} = {AC[12], AC[4]};

  // Other names for the same wires on the sheet: AC_0 = AC[0]; AC_15 = AC[15]

  // Notes on the sheet:
  //   ALU
endmodule
