// Digital circuit alu_one_stage.dig as structural Verilog
module alu_one_stage (
  input  AC_i,
  input  DR_i,
  input  C_i,
  input  AC_i_plus_1,
  input  AC_i_1,
  output Ii,
  output C_i_plus_1
);

  wire and_1_out, and_2_out, and_3_out, and_4_out, and_6_out, and_7_out, and_8_out, and_9_out, and_10_out,
       and_11_out, and_12_out, D0, D1, D3, D4, not_1_out, or_1_out, or_2_out, P1, P8, P9, r, sub_1_s;
  wire [15:0] add_1_s, and_5_out, D2, T5;

  Add add_1 (.a(AC_i), .b(AC_i), .c_i(C_i), .s(add_1_s[0]), .c_o(C_i_plus_1));
  Sub sub_1 (.a(AC_i), .b(DR_i), .c_i(C_i), .s(sub_1_s), .c_o(C_i_plus_1));
  and and_1 (and_1_out, r, P1);
  and and_2 (and_2_out, r, P8);
  and and_3 (and_3_out, r, P9);
  and and_4 (and_4_out, T5[0], D0, AC_i, DR_i);
  assign and_5_out = T5 & add_1_s & D2;  // And and_5, 16 bits wide
  and and_6 (and_6_out, DR_i, T5[0], D4);
  or or_1 (or_1_out, DR_i, AC_i);
  and and_7 (and_7_out, T5[0], D1);
  and and_8 (and_8_out, sub_1_s, T5[0], D3);
  and and_9 (and_9_out, not_1_out, and_1_out);
  not not_1 (not_1_out, AC_i);
  and and_10 (and_10_out, AC_i_plus_1, and_2_out);
  and and_11 (and_11_out, AC_i_1, and_3_out);
  and and_12 (and_12_out, or_1_out, and_7_out);
  or or_2 (or_2_out, and_10_out, and_11_out);
  or or_3 (Ii, and_4_out, and_5_out[0], and_6_out, and_12_out, and_8_out, and_9_out, or_2_out);
  // Pins of 1 and 16 bits meet at T5
  // Pins of 1 and 16 bits meet at add_1_s
  // Pins of 1 and 16 bits meet at and_5_out

  // Notes on the sheet:
  //   ALU
endmodule
