// Digital circuit ar_control.dig as structural Verilog
module ar_control (
  output ld,
  output clr,
  output INR
);

  wire and_3_out, and_4_out, D7, I0, I1, or_1_out, R, R_t, T0, T2, T3, T5;

  or or_1 (or_1_out, T0, T2);
  and and_1 (INR, D7, T5);
  and and_2 (clr, R, T0);
  and and_3 (and_3_out, R_t, or_1_out);
  and and_4 (and_4_out, I0, I1, T3);
  or or_2 (ld, and_3_out, and_4_out);
endmodule
