// Digital circuit bus_selection_lines.dig as structural Verilog
module bus_selection_lines (
  output sel0,
  output sel1,
  output sel2
);

  wire memory_selection_logic_1_mem, selection_logic_for_ac_1_ac, selection_logic_for_ar_1_ar,
       selection_logic_for_dr_1_dr, selection_logic_for_ir_1_ir, selection_logic_for_pc_1_pc,
       seletion_logic_for_tr_1_tr;

  selection_logic_for_AR selection_logic_for_ar_1 (.AR(selection_logic_for_ar_1_ar));
  selection_logic_for_PC selection_logic_for_pc_1 (.PC(selection_logic_for_pc_1_pc));
  selection_logic_for_DR selection_logic_for_dr_1 (.DR(selection_logic_for_dr_1_dr));
  selection_logic_for_AC selection_logic_for_ac_1 (.AC(selection_logic_for_ac_1_ac));
  selection_logic_for_IR selection_logic_for_ir_1 (.IR(selection_logic_for_ir_1_ir));
  seletion_logic_for_TR seletion_logic_for_tr_1 (.TR(seletion_logic_for_tr_1_tr));
  Memory_selection_logic memory_selection_logic_1 (.Mem(memory_selection_logic_1_mem));
  PriorityEncoder #(.Selector_Bits(3)) priorityencoder_1 (
    .in0(1'b0), .in1(selection_logic_for_ar_1_ar), .in2(selection_logic_for_pc_1_pc),
    .in3(selection_logic_for_dr_1_dr), .in4(selection_logic_for_ac_1_ac), .in5(selection_logic_for_ir_1_ir),
    .in6(seletion_logic_for_tr_1_tr), .in7(memory_selection_logic_1_mem), .num({sel2, sel1, sel0}));  // open: any
endmodule
