// Digital circuit computer.dig as structural Verilog
module computer (
  input  clk
);

  instruction_decoder instruction_decoder_1 ();  // open: IR_0, IR_1, IR_2, IR_3, IR_4, IR_5, IR_6, IR_7, IR_8, IR_9, IR_10, IR_11, IR_12, IR_13, IR_14, IR_15

  // Other names for the same wires on the sheet: Master_Clock = clk
endmodule
