// Digital circuit dr_control.dig as structural Verilog
module dr_control (
  output ld,
  output clr,
  output INR
);

  wire and_2_out, and_3_out, and_4_out, D8, I0, I0_t, I1, I1_t, T5;

  and and_1 (INR, D8, T5);
  and and_2 (and_2_out, I0, I1_t);
  and and_3 (and_3_out, I0, I1);
  and and_4 (and_4_out, I0_t, I1);
  or or_1 (ld, and_2_out, and_3_out, and_4_out);

  assign clr = 1'b0;
endmodule
