// Digital circuit e_flag.dig as structural Verilog
module e_flag (
  input  Cout,
  input  AC_0,
  input  AC_15,
  output E
);

  wire and_1_out, and_2_out, and_3_out, and_4_out, and_5_out, and_6_out, and_7_out, and_8_out, and_9_out,
       and_10_out, and_11_out, D2, E_t, Master_Clock, not_1_out, not_2_out, not_3_out, not_4_out, or_1_out,
       or_2_out, P5, P6, P8, P9, r, T5;

  and and_1 (and_1_out, D2, T5);
  not not_1 (not_1_out, E_t);
  and and_2 (and_2_out, D2, T5);
  not not_2 (not_2_out, Cout);
  and and_3 (and_3_out, r, P5);
  not not_3 (not_3_out, AC_0);
  not not_4 (not_4_out, AC_15);
  and and_4 (and_4_out, and_1_out, Cout);
  and and_5 (and_5_out, r, P6, not_1_out);
  and and_6 (and_6_out, r, P8, AC_0);
  and and_7 (and_7_out, r, P9, AC_15);
  and and_8 (and_8_out, and_2_out, not_2_out);
  and and_9 (and_9_out, r, P6, E_t);
  and and_10 (and_10_out, r, P8, not_3_out);
  and and_11 (and_11_out, r, P9, not_4_out);
  or or_1 (or_1_out, and_4_out, and_5_out, and_6_out, and_7_out);
  or or_2 (or_2_out, and_8_out, and_3_out, and_9_out, and_10_out, and_11_out);
  JK_FF jk_ff_1 (.J(or_1_out), .C(Master_Clock), .K(or_2_out), .Q(E));  // open: nQ
endmodule
