// Digital circuit fgi_flag.dig as structural Verilog
module fgi_flag (
  output FGI
);

  wire and_1_out, Master_Clock, P0, q;

  and and_1 (and_1_out, q, P0);
  JK_FF jk_ff_1 (.J(1'b0), .C(Master_Clock), .K(and_1_out), .Q(FGI));  // open: nQ
endmodule
