// Digital circuit fgo_flag.dig as structural Verilog
module fgo_flag (
  output FGO
);

  wire and_1_out, Mater_Clock, P1, q;

  and and_1 (and_1_out, q, P1);
  JK_FF jk_ff_1 (.J(1'b0), .C(Mater_Clock), .K(and_1_out), .Q(FGO));  // open: nQ
endmodule
