// Digital circuit i0_flag.dig as structural Verilog
module i0_flag (
  input  IR_15,
  output I0
);

  wire and_1_out, and_2_out, Master_Clock, not_1_out, R, T2;

  not not_1 (not_1_out, IR_15);
  and and_1 (and_1_out, IR_15, R, T2);
  and and_2 (and_2_out, R, T2, not_1_out);
  JK_FF jk_ff_1 (.J(and_1_out), .C(Master_Clock), .K(and_2_out), .Q(I0));  // open: nQ
endmodule
