// Digital circuit ien_flag.dig as structural Verilog
module ien_flag (
  output IEN
);

  wire and_1_out, and_2_out, and_3_out, Mater_Clock, or_1_out, p2, P3, q, R, T2;

  and and_1 (and_1_out, q, p2);
  and and_2 (and_2_out, R, T2);
  and and_3 (and_3_out, q, P3);
  or or_1 (or_1_out, and_2_out, and_3_out);
  JK_FF jk_ff_1 (.J(and_1_out), .C(Mater_Clock), .K(or_1_out), .Q(IEN));  // open: nQ
endmodule
