// Digital circuit instruction_decoder.dig as structural Verilog
module instruction_decoder (
);

  wire D0, D1, D2, D3, D4, D5, D6, D7, D8, D9, D10, D11, D12, D13, D14, D15, I, I0, I0_t, I1, I1_t, I_t, IR0,
       IR1, IR2, IR3, IR10, IR11, IR12, IR13, P0, P1, P2, P3, P4, P5, P6, P7, P8, P9, P10, P11, P12, P13,
       P14, P15, q, R, R_t, r_t_t, T3;

  not not_1 (I_t, I);
  Decoder #(.Selector_Bits(4)) decoder_1 (
    .sel({IR10, IR11, IR12, IR13}), .out_0(D0), .out_1(D1), .out_2(D2), .out_3(D3), .out_4(D4), .out_5(D5),
    .out_6(D6), .out_7(D7), .out_8(D8), .out_9(D9), .out_10(D10), .out_11(D11), .out_12(D12), .out_13(D13),
    .out_14(D14), .out_15(D15));
  not not_2 (I1_t, I1);
  not not_3 (R_t, R);
  Decoder #(.Selector_Bits(4)) decoder_2 (
    .sel({IR0, IR1, IR2, IR3}), .out_0(P0), .out_1(P1), .out_2(P2), .out_3(P3), .out_4(P4), .out_5(P5),
    .out_6(P6), .out_7(P7), .out_8(P8), .out_9(P9), .out_10(P10), .out_11(P11), .out_12(P12), .out_13(P13),
    .out_14(P14), .out_15(P15));
  not not_4 (I0_t, I0);
  and and_1 (r_t_t, D0, I0_t, I1_t, T3);
  and and_2 (q, D15, I0_t, I1_t, T3);

  // Notes on the sheet:
  //   T0
  //   T1
  //   I
  //   T2
  //   T3
  //   I1
  //   T4
  //   T5
  //   R
  //   I0
  //   T6
endmodule
