// Digital circuit memory_control.dig as structural Verilog
module memory_control (
  output Write,
  output Read
);

  wire and_1_out, and_2_out, and_3_out, and_4_out, and_5_out, and_6_out, D0, D1, D2, D3, D5, D6, D7, I,
       not_1_out, or_1_out, or_2_out, R, R_t, T1, T3, T4, T6;

  not not_1 (not_1_out, D7);
  or or_1 (or_1_out, D3, D5);
  or or_2 (or_2_out, D0, D1, D2, D3);
  and and_1 (and_1_out, R, T1);
  and and_2 (and_2_out, T4, or_1_out);
  and and_3 (and_3_out, D6, T6);
  and and_4 (and_4_out, R_t, T1);
  and and_5 (and_5_out, not_1_out, I, T3);
  and and_6 (and_6_out, T4, or_2_out);
  or or_3 (Write, and_1_out, and_2_out, and_3_out);
  or or_4 (Read, and_4_out, and_5_out, and_6_out);
endmodule
