// Digital circuit pc_control.dig as structural Verilog
module pc_control (
  output ld,
  output clr,
  output INR
);

  wire and_1_out, and_2_out, and_3_out, and_4_out, and_5_out, and_6_out, and_7_out, D6, D7, D8, or_1_out,
       or_2_out, P2, P3, P4, P5, P7, q, R, R_t, r_t_t, T1, T2, T5, T6;

  and and_1 (and_1_out, R, T2);
  and and_2 (and_2_out, R_t, T1);
  or or_1 (or_1_out, P4, P5);
  or or_2 (or_2_out, P2, P3, P4, P7);
  and and_3 (and_3_out, D6, T5);
  and and_4 (and_4_out, D7, T6);
  and and_5 (and_5_out, D8, T6);
  and and_6 (and_6_out, or_1_out, q);
  and and_7 (and_7_out, or_2_out, r_t_t);
  and and_8 (clr, R, T1);
  or or_3 (ld, and_3_out, and_4_out);
  or or_4 (INR, and_5_out, and_1_out, and_2_out, and_6_out, and_7_out);
endmodule
