// Digital circuit r_flag.dig as structural Verilog
module r_flag (
  output R
);

  wire and_1_out, and_2_out, and_3_out, and_4_out, FGI, FGO, IEN, Master_Clock, or_1_out, R_t, T0, T1, T2,
       T2_t;

  and and_1 (and_1_out, T0, T1, T2_t);
  and and_2 (and_2_out, IEN, and_1_out);
  or or_1 (or_1_out, FGI, FGO);
  and and_3 (and_3_out, R_t, T2);
  and and_4 (and_4_out, and_2_out, or_1_out);
  JK_FF jk_ff_1 (.J(and_4_out), .C(Master_Clock), .K(and_3_out), .Q(R));  // open: nQ
endmodule
