// Digital circuit register_with_increment.dig as structural Verilog
module register_with_increment (
  input  INR,
  input  CLK,
  input  [9:0] Din,
  input  ld,
  input  clr,
  output [9:0] D
);

  CounterPreset #(.Bits(10)) counterpreset_1 (
    .en(INR), .C(CLK), .dir(1'b0), .in(Din), .ld(ld), .clr(clr), .out(D));  // open: ovf
endmodule
