// Digital circuit sc_control.dig as structural Verilog
module sc_control (
  output clr
);

  wire and_1_out, and_2_out, and_3_out, D0, D1, D2, D3, D4, D5, D6, D7, D8, or_1_out, or_2_out, q, R, r_t,
       T2, T5, T6;

  and and_1 (and_1_out, R, T2);
  or or_1 (or_1_out, D0, D1, D2, D3, D4, D5, D6);
  or or_2 (or_2_out, D7, D8);
  and and_2 (and_2_out, T5, or_1_out);
  and and_3 (and_3_out, T6, or_2_out);
  or or_3 (clr, and_1_out, r_t, and_2_out, q, and_3_out);
endmodule
