// Digital circuit selection_logic_for_AC.dig as structural Verilog
module selection_logic_for_AC (
  output out_1
);

  wire and_1_out, and_2_out, and_3_out, D0, D1, D3, T4, T5;

  and and_1 (and_1_out, D0, T5);
  and and_2 (and_2_out, D1, T5);
  and and_3 (and_3_out, D3, T4);
  or or_1 (out_1, and_1_out, and_2_out, and_3_out);
endmodule
