// Digital circuit selection_logic_for_AR.dig as structural Verilog
module selection_logic_for_AR (
  output out_1
);

  wire and_1_out, and_2_out, D7, I0, I1, T4, T5;

  and and_1 (and_1_out, I0, I1, T4);
  and and_2 (and_2_out, D7, T5);
  or or_1 (out_1, and_1_out, and_2_out);
endmodule
