// Digital circuit selection_logic_for_DR.dig as structural Verilog
module selection_logic_for_DR (
  output out_1
);

  wire and_1_out, and_2_out, and_3_out, and_4_out, and_5_out, D0, D1, D2, D6, T5, T6;

  and and_1 (and_1_out, D6, T6);
  and and_2 (and_2_out, D6, T5);
  and and_3 (and_3_out, D0, T5);
  and and_4 (and_4_out, D1, T5);
  and and_5 (and_5_out, D2, T5);
  or or_1 (out_1, and_1_out, and_2_out, and_3_out, and_4_out, and_5_out);
endmodule
