// Digital circuit tr_control.dig as structural Verilog
module tr_control (
  output ld,
  output clr,
  output INR
);

  wire R, T0;

  and and_1 (ld, T0, R);

  assign clr = 1'b0;
  assign INR = 1'b0;
endmodule
